# Fritzing sketch spires (saved by Fritzing 1.0.3b)
circuit board: 5.7cm x 6.1cm
breadboards: 2

parts:
  Nano = Arduino Nano (Rev3.0)
  RE1 = Rotary Encoder [package=THT]
  S5 = SPST Switch [package=switch-spdt_kit]
  A1 = VL53lox
  U1 = AD9833 Module
  VCC1 = 4 x AAA Battery Mount
  LDR5 = Photocell (LDR) [power=0.25W dark_resistance_@0.01lx=300kΩ light_resistance_@100lx=400Ω luminance=10lx package=THT]
  LED8 = LED - 3mm [color="Red (635nm)" current=0.030A package="3 mm [THT]"]  # not connected
  1K = Resistor [tolerance=±5% resistance=1k power=0.25W package=THT]  # not connected
  100uF1 = Electrolytic Capacitor [capacitance=0.1mF voltage=35V package="100 mil [THT, electrolytic]"]
  100K = Resistor [tolerance=±5% resistance=100k power=0.25W package=THT]
  LM387 = LM386 [package=dip08]
  SPKR1 = Loudspeaker
  100uf = Electrolytic Capacitor [capacitance=0.1mF voltage=35V package="100 mil [THT, electrolytic]"]
  10uf = Electrolytic Capacitor [capacitance=10µF voltage=35V package="100 mil [THT, electrolytic]"]
  10uf_2 = Electrolytic Capacitor [capacitance=10µF voltage=35V package="100 mil [THT, electrolytic]"]
  104 = Ceramic Capacitor [capacitance=100nF voltage=16V package="200 mil [THT, multilayer]"]
  104_2 = Ceramic Capacitor [capacitance=100nF voltage=16V package="200 mil [THT, multilayer]"]
  470pf = Ceramic Capacitor [capacitance=0.47nF voltage=16V package="200 mil [THT, multilayer]"]
  out2 = Audio Jack (TRS) 3.5mm [package="PG203J [THT]"]
  10 = Resistor [tolerance=±5% resistance=10 power=0.25W package=THT]
  10K = Resistor [tolerance=±5% resistance=10k power=0.25W package=THT]
  1-10K1 = Rotary Potentiometer (Small) [maximum_resistance=10kΩ knob_status=50% power=0.5W package=THT]
  10K3 = Resistor [tolerance=±5% resistance=10k power=0.25W package=THT]
  104_3 = Ceramic Capacitor [capacitance=100nF voltage=16V package="200 mil [THT, multilayer]"]
  J5 = 3.5mm Audio Jack-wq-pj320b.fzpz [package=audio-jack-3.5mm-smd]  # not connected
  104_4 = Ceramic Capacitor [capacitance=100nF voltage=16V package="200 mil [THT, multilayer]"]

nets:
  GND: Nano.GND, RE1.GND, RE1.SW-2, A1.Pin_2, U1.DGND
  N1: Nano.D4, RE1.SW-1
  N2: Nano.D5, RE1.Pin-B
  N3: Nano.D6, RE1.Pin-A
  N4: Nano.VIN, S5.S
  V++: Nano.5V, U1.VCC, 100uF1.+, LM387.V+, 104_3.1, 104_4.0
  N5: Nano.A5, A1.Pin_3
  N6: Nano.A4, A1.Pin_4
  N7: Nano.3V3, A1.Pin_1
  N8: S5.P, VCC1.+
  N9: U1.AGND, VCC1.-, 100uF1.-, 100K.Pin_1, LM387.-IN, LM387.V-, SPKR1.pin1, 10uf.-, 470pf.0, 470pf.1, out2.Sleeve, 10.Pin_0, 1-10K1.leg1, 104_3.0, 104_4.1
  N10: U1.OUT, 104.1
  N11: LDR5.pin_0, 100K.Pin_0, 104.0
  N12: LDR5.pin_1, 1-10K1.leg2
  N13: LM387.GAIN, 10uf_2.-, 10K3.Pin_0
  N14: LM387.+IN, 1-10K1.wiper
  N15: LM387.OUT, 100uf.+, 104_2.1
  N16: LM387.BP, 10K.Pin_0
  N17: SPKR1.pin2, 100uf.-, out2.Ring
  N18: 10uf.+, 10K.Pin_1
  N19: 10uf_2.+, 10K3.Pin_1
  N20: 104_2.0, 10.Pin_1

notes:
  blueprint@poetaster.de 2025
  spires v1

custom parts:
  Rotary Encoder: Rotary Encoder with push button
  VL53lox: VL53L0X Time-of-Flight (ToF) Laser Ranging Sensor Breakout.
  AD9833 Module: programmable waveform generator
  4 x AAA Battery Mount: A 4 x AAA battery pack (4.8 Volts with recharables)
  3.5mm Audio Jack-wq-pj320b.fzpz: 3.5mm Audio Jack WQP-PJ320B is a SMD jack, dia 1/8 inch, female, right angle and through hole.
